// Logisim project source.circ as structural Verilog: 11 circuits, main circuit source
module source (
  input  in_1,
  output halt,
  output [31:0] out_3,
  output out_4,
  output [4:0] out_5,
  output [31:0] out_6,
  output out_7,
  output [4:0] out_8,
  output [31:0] out_9,
  output [31:0] out_10
);

  wire ALU_B_sel, clk, clock_1_out, cmp, comparator_1_eq;
  wire [1:0] EXT_op, RF_A3_sel, RF_WD_sel;
  wire [2:0] MR_op, MW_op, NPC_op;
  wire [3:0] ALU_op;
  wire [4:0] istr_15_11, istr_20_16, istr_25_21, Shamt;
  wire [9:0] counter_1_q;
  wire [15:0] imm16;
  wire [25:0] imm26;
  wire [31:0] ALU_C, DM_RD, EXTout, MR_Out, multiplexer_4_out, npc_1_out_6, PC4, RF_RD1, RF_RD2;

  Clock clock_1 (.out(clock_1_out));
  Counter #(.width(10), .max('h3ff), .ongoal("stay")) counter_1 (
    .Q(counter_1_q), .carry(halt), .clk(clock_1_out));  // open: load, D, count, clr
  Comparator #(.width(10), .mode("unsigned")) comparator_1 (
    .a(counter_1_q), .b(10'h180), .eq(comparator_1_eq));  // open: gt, lt
  Multiplexer multiplexer_1 (.in0(clock_1_out), .in1(1'b0), .out(clk), .sel(comparator_1_eq));  // open: en
  Register #(.width(32)) PC (.D(npc_1_out_6), .Q(out_10), .clk(clk), .clr(in_1));  // open: en
  NPC npc_1 (.out_6(npc_1_out_6), .in_4(out_10), .in_5(RF_RD1), .in_1(imm26), .in_2(NPC_op), .in_3(cmp), .PC4(PC4));
  IM im_1 (.in_1(out_10), .out_2(out_3));
  SPLT splt_1 (
    .in_1(out_3), .out_2(imm26), .out_3(imm16), .out_4(istr_25_21), .out_5(istr_20_16), .out_6(istr_15_11),
    .out_7(Shamt));
  CTR ctr_1 (
    .in_1(out_3), .out_2(NPC_op), .out_3(out_4), .out_4(RF_A3_sel), .out_5(RF_WD_sel), .out_6(EXT_op),
    .out_7(ALU_op), .out_8(ALU_B_sel), .out_9(out_7), .out_10(MW_op), .out_11(MR_op));
  EXT ext_1 (.in_2(imm16), .out_3(EXTout), .in_1(EXT_op));
  Multiplexer #(.select(2), .width(5)) multiplexer_2 (
    .in0(istr_20_16), .in1(istr_15_11), .in2({5{1'b1}}), .out(out_5), .sel(RF_A3_sel));  // open: in3, en
  RF rf_1 (
    .A1(istr_25_21), .A2(istr_20_16), .A3(out_5), .out_8(RF_RD1), .out_9(RF_RD2), .clk(clk), .WE(out_4),
    .reset(in_1), .in_7(out_6));
  Multiplexer #(.select(2), .width(32)) multiplexer_3 (
    .in0({ALU_C[31:7], out_8, ALU_C[1:0]}), .in1(MR_Out), .in2(PC4), .in3(EXTout), .out(out_6),
    .sel(RF_WD_sel));  // open: en
  Multiplexer #(.width(32)) multiplexer_4 (
    .in0(RF_RD2), .in1(EXTout), .out(multiplexer_4_out), .sel(ALU_B_sel));  // open: en
  ALU alu_1 (
    .in_3(RF_RD1), .in_4(multiplexer_4_out), .out_5({ALU_C[31:7], out_8, ALU_C[1:0]}), .in_1(ALU_op),
    .in_2(Shamt), .out_6(cmp));
  MW mw_1 (.in_3({ALU_C[31:7], out_8, ALU_C[1:0]}), .in_4(RF_RD2), .Out(out_9), .in_1(MW_op), .in_2(DM_RD));
  DM dm_1 (.in_4(out_8), .out_6(DM_RD), .in_1(out_7), .in_2(clk), .in_3(in_1), .in_5(out_9));
  MR mr_1 (.in_2({ALU_C[31:7], out_8, ALU_C[1:0]}), .in_3(DM_RD), .Out(MR_Out), .in_1(MR_op));

  // Other names for the same wires on the sheet: ALU_C[6:2] = out_8; DMaddr[4:0] = out_8; DM_wr = out_7;
  //   Istr[31:0] = out_3; MW_Out[31:0] = out_9; pc[31:0] = out_10; res = in_1; RF_WD[31:0] = out_6; RF_wr = out_4;
  //   RFaddr[4:0] = out_5

  // Notes on the sheet:
  //   CPU(mips sig_circ)
endmodule

module RF (
  input  clk,
  input  WE,
  input  reset,
  input  [4:0] A1,
  input  [4:0] A2,
  input  [4:0] A3,
  input  [31:0] in_7,
  output [31:0] out_8,
  output [31:0] out_9
);

  wire in00, in01, in02, in03, in04, in05, in06, in07, in08, in09, in10, in11, in12, in13, in14, in15, in16,
       in17, in18, in19, in20, in21, in22, in23, in24, in25, in26, in27, in28, in29, in30, in31;
  wire [31:0] out00, out01, out02, out03, out04, out05, out06, out07, out08, out09, out10, out11, out12,
       out13, out14, out15, out16, out17, out18, out19, out20, out21, out22, out23, out24, out25, out26,
       out27, out28, out29, out30, out31;

  Register #(.width(32)) register_1 (.D({32{1'b0}}), .en(in00), .Q(out00), .clk(clk), .clr(reset));
  Register #(.width(32)) register_2 (.D(in_7), .en(in08), .Q(out08), .clk(clk), .clr(reset));
  Register #(.width(32)) register_3 (.D(in_7), .en(in16), .Q(out16), .clk(clk), .clr(reset));
  Register #(.width(32)) register_4 (.D(in_7), .en(in24), .Q(out24), .clk(clk), .clr(reset));
  Demultiplexer #(.select(5), .disabled(0), .enable("false")) demultiplexer_1 (
    .out0(in00), .out1(in01), .out2(in02), .out3(in03), .out4(in04), .out5(in05), .out6(in06), .out7(in07),
    .out8(in08), .out9(in09), .out10(in10), .out11(in11), .out12(in12), .out13(in13), .out14(in14),
    .out15(in15), .out16(in16), .out17(in17), .out18(in18), .out19(in19), .out20(in20), .out21(in21),
    .out22(in22), .out23(in23), .out24(in24), .out25(in25), .out26(in26), .out27(in27), .out28(in28),
    .out29(in29), .out30(in30), .out31(in31), .in(WE), .sel(A3));
  Register #(.width(32)) register_5 (.D(in_7), .en(in01), .Q(out01), .clk(clk), .clr(reset));
  Register #(.width(32)) register_6 (.D(in_7), .en(in09), .Q(out09), .clk(clk), .clr(reset));
  Register #(.width(32)) register_7 (.D(in_7), .en(in17), .Q(out17), .clk(clk), .clr(reset));
  Register #(.width(32)) register_8 (.D(in_7), .en(in25), .Q(out25), .clk(clk), .clr(reset));
  Register #(.width(32)) register_9 (.D(in_7), .en(in02), .Q(out02), .clk(clk), .clr(reset));
  Register #(.width(32)) register_10 (.D(in_7), .en(in10), .Q(out10), .clk(clk), .clr(reset));
  Register #(.width(32)) register_11 (.D(in_7), .en(in18), .Q(out18), .clk(clk), .clr(reset));
  Register #(.width(32)) register_12 (.D(in_7), .en(in26), .Q(out26), .clk(clk), .clr(reset));
  Register #(.width(32)) register_13 (.D(in_7), .en(in03), .Q(out03), .clk(clk), .clr(reset));
  Register #(.width(32)) register_14 (.D(in_7), .en(in11), .Q(out11), .clk(clk), .clr(reset));
  Register #(.width(32)) register_15 (.D(in_7), .en(in19), .Q(out19), .clk(clk), .clr(reset));
  Register #(.width(32)) register_16 (.D(in_7), .en(in27), .Q(out27), .clk(clk), .clr(reset));
  Multiplexer #(.select(5), .width(32), .enable("false")) multiplexer_1 (
    .in0(out00), .in1(out01), .in2(out02), .in3(out03), .in4(out04), .in5(out05), .in6(out06), .in7(out07),
    .in8(out08), .in9(out09), .in10(out10), .in11(out11), .in12(out12), .in13(out13), .in14(out14),
    .in15(out15), .in16(out16), .in17(out17), .in18(out18), .in19(out19), .in20(out20), .in21(out21),
    .in22(out22), .in23(out23), .in24(out24), .in25(out25), .in26(out26), .in27(out27), .in28(out28),
    .in29(out29), .in30(out30), .in31(out31), .out(out_8), .sel(A1));
  Register #(.width(32)) register_17 (.D(in_7), .en(in04), .Q(out04), .clk(clk), .clr(reset));
  Register #(.width(32)) register_18 (.D(in_7), .en(in12), .Q(out12), .clk(clk), .clr(reset));
  Register #(.width(32)) register_19 (.D(in_7), .en(in20), .Q(out20), .clk(clk), .clr(reset));
  Register #(.width(32)) register_20 (.D(in_7), .en(in28), .Q(out28), .clk(clk), .clr(reset));
  Register #(.width(32)) register_21 (.D(in_7), .en(in05), .Q(out05), .clk(clk), .clr(reset));
  Register #(.width(32)) register_22 (.D(in_7), .en(in13), .Q(out13), .clk(clk), .clr(reset));
  Register #(.width(32)) register_23 (.D(in_7), .en(in21), .Q(out21), .clk(clk), .clr(reset));
  Register #(.width(32)) register_24 (.D(in_7), .en(in29), .Q(out29), .clk(clk), .clr(reset));
  Multiplexer #(.select(5), .width(32), .enable("false")) multiplexer_2 (
    .in0(out00), .in1(out01), .in2(out02), .in3(out03), .in4(out04), .in5(out05), .in6(out06), .in7(out07),
    .in8(out08), .in9(out09), .in10(out10), .in11(out11), .in12(out12), .in13(out13), .in14(out14),
    .in15(out15), .in16(out16), .in17(out17), .in18(out18), .in19(out19), .in20(out20), .in21(out21),
    .in22(out22), .in23(out23), .in24(out24), .in25(out25), .in26(out26), .in27(out27), .in28(out28),
    .in29(out29), .in30(out30), .in31(out31), .out(out_9), .sel(A2));
  Register #(.width(32)) register_25 (.D(in_7), .en(in06), .Q(out06), .clk(clk), .clr(reset));
  Register #(.width(32)) register_26 (.D(in_7), .en(in14), .Q(out14), .clk(clk), .clr(reset));
  Register #(.width(32)) register_27 (.D(in_7), .en(in22), .Q(out22), .clk(clk), .clr(reset));
  Register #(.width(32)) register_28 (.D(in_7), .en(in30), .Q(out30), .clk(clk), .clr(reset));
  Register #(.width(32)) register_29 (.D(in_7), .en(in07), .Q(out07), .clk(clk), .clr(reset));
  Register #(.width(32)) register_30 (.D(in_7), .en(in15), .Q(out15), .clk(clk), .clr(reset));
  Register #(.width(32)) register_31 (.D(in_7), .en(in23), .Q(out23), .clk(clk), .clr(reset));
  Register #(.width(32)) register_32 (.D(in_7), .en(in31), .Q(out31), .clk(clk), .clr(reset));

  // Other names for the same wires on the sheet: RD1[31:0] = out_8; RD2[31:0] = out_9; WD[31:0] = in_7
endmodule

module IM (
  input  [31:0] in_1,
  output [31:0] out_2
);

  ROM #(.addrWidth(10), .dataWidth(32)) rom_1 (.addr(in_1[11:2]), .data(out_2));  // open: sel

  // Notes on the sheet:
  //   contents of rom_1 (hex, n*v repeats v):
  //   03fff823 00000000 00052d40 001ff82a 03c1f82a 03e40821 00000000 ac000038 00000000 ac01001c 00a1002a
  //   03e3082a 8c1f0070 ac000058 24652547 005ff023 27df0d9f 00031640 00000000 00822023 00000000 0004f580
  //   8c04006c 00000000 00621821 03c1f021 00852021 ac00004c 00000000 007ef024 3c1f9d27 ac1f0024 3c022cdb
  //   03e21821 ac030074 00000000 00000000 8c040058 247e4e9e 00000000 34a33df7 8c040004 24227f9f 24a45a06
  //   00002021 00000000 349fbe16 27e00951 03df0023 0000f680 0081f824 005f0023 03de282a 348292d9 242231e4
  //   34856b7f 00000000 001ff023 03c1f82a 007e2023 007f0023 8c000074 00000000 00000000 03e0f821 3c01e1d3
  //   8c050020 00030823 0084f82a 00000000 00851824 3c1e6b41 37e51787 0005f500 00642821 0025f021 0042182a
  //   00000000 8c010030 0083102a 00000000 00000000 00000000 24024ff4 341f4fe0 001ef500 00bff824 00611023
  //   34be938b 8c030034 009ef82a 00000000 10a0001e 00000000 00000000 103f0028 3c042151 37ffd366 ac040004
  //   08000070 3c01645d 24204fc8 24654882 000420c0 24200ce3 37de6970 00251821 241e6831 24036653 00012024
  //   10650023 34a53ba0 0c000086 ac1f0048 08000085 03e2002a 03c51824 003e0023 27de335f 27e009b8 24bf19d9
  //   08000086 03e5f02a 00000000 3461dd59 00000000 ac01000c 00031f40 000526c0 00011c00 03e1002a 00a22824
  //   ac1e0054 8c030024 005ef824 00a4082a 34804e00 00a02021 0064f024 0065182a 00000000 080000b5 3c0159d2
  //   24a02d98 0020f82a 1060001d 3c05d36e 00000000 007f0021 34a48f06 8c050064 00832823 03c3f024 27e560a8
  //   0040f024 0c0000c8 0004f200 8c020064 00000000 ac010030 00200023 080000ab 34056995 8c1e0060 0020f821
  //   8c040028 24be0437 009ef02a 8c040034 13df0015 24a017ed ac020078 080000c7 3c0022d8 3c03848a 03c51821
  //   3c03d5d1 ac01005c 00000000 0044082a 00a5f021 0065182a 00431023 8c04003c 00000000 00000000 3c039942
  //   0c0000ce 03e0f824 8c020060 13df001b 00000000 0c0000e6 ac010040 0c0000e9 ac020048 00a5282a 27de47b0
  //   00000000 8c040004 8c030018 000103c0 0c0000d7 8c02006c 00a2102a 24022207 34617ef4 8c1f0058 37e49706
  //   3c04858f 00000000 00452821 00000000 00000000 ac040064 00000000 080000f0 03c5182a 00821024 00a01023
  //   13c30012 3461aba3 00050500 03c4082a 00820024 24a352d7 0c000103 34be8642 1084002d 00000000 00012400
  //   10a40016 00000000 0c0000f1 24840d88 ac010078 0c0000fa 001e0023 1043002f 0042f824 00000600 08000118
  //   0082102a 00430821 00000000 00000000 001f1023 00000000 0800011d 00000000 08000103 8c050078 003e1024
  //   37e00e1d 009ff02a 0800012d 00000000 00411821 00000000 00a51023 ac010008 ac050030 00050600 34648acb
  //   0c00012d 00430024 0800013a 00000000 34825778 03c1f824 343f2f33 00000000 0005f824 27e45a39 10220014
  //   37c2bcdf 00000000 341edab8 00000000 0041f821 00000000 00041840 00000000 00650824 00000000 005e0824
  //   03e2202a 03e5082a 001e1180 03e32823 08000141 001e0940 243f33de 0800012c 8c030060 08000159 00000000
  //   2402530e ac02004c 00000000 00000000 3c035087 00012024 8c040024 34a04fcb 27c33253 0082102a 00000000
  //   2403184d 3421cb68 8c1e0040 37df959c 3c04b085 3c05b03c 34454983 ac03005c 3c0173c9 00000000 00000000
  //   8c1e0040 0004f540 00bef823 0061182a 00422024 03e10824 00a5f824 1084002c 0021f824 8c1f0020 03e3f024
  //   00000000 08000164 001e1300 00852823 0001f040 009e202a 0c000159 27e03e8d 00000000 10a20000 ac1e0000
  //   8c00002c 00a12023 8c000054 10400001 8c040024 00000000 03c31823 8c02001c 00000000 00012021 0083282a
  //   8c1e0074 00000000 00022024 08000164 00000000 349e8647 ac1e006c 0800016f ac050048 00030a40 37c28f3f
  //   0061282a 08000186 00020021 8c010068 24842e4f 08000190 00021680 34a03dff 0042f821 003f0824 342583f3
  //   00012380 00000000 00000000 007f2021 00000000 ac1f0038 10210016 00000000 37e5bac8 13c50013 8c04002c
  //   00000000 00000000 00000000 00032100 00000000 10020020 245e4f8b 3c03d049 0c0001a9 00a0f82a 00402821
  //   0004f824 03e02024 0005f02a 00641821 0c0001c0 03def023 13e20002 3c017886 00000000 103f002c 00000000
  //   0c0001c0 00000000 1024000b 0003f82a 001e0740 00000000 00bef823 00000000 1004000d 00000000 13c00004
  //   0002f82a 0c0001ae 003f282a 00000000 0004f440 00000000 03fff82a 00000000 0c0001ad 03c02021 00041823
  //   8c03001c 345f8598 080001c0 ac1e004c 03fe1021 ac000060 00000000 24bf3993 10bf0018 00040200 080001c2
  //   00201821 8c050034 00000000 ac1f0004 0c00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
endmodule

module NPC (
  input  [25:0] in_1,
  input  [2:0] in_2,
  input  in_3,
  input  [31:0] in_4,
  input  [31:0] in_5,
  output [31:0] out_6,
  output [31:0] PC4
);

  wire [31:0] adder_2_out, beq_bgez, bit_extender_1_out;

  Adder #(.width(32)) adder_1 (.a(in_4), .b(32'h4), .out(PC4));  // open: cin, cout
  assign bit_extender_1_out = {{14{in_1[15]}}, {in_1[15:0], 2'b00}};  // Bit_Extender bit_extender_1
  Multiplexer #(.width(32), .enable("false")) multiplexer_1 (.in0(PC4), .in1(adder_2_out), .out(beq_bgez), .sel(in_3));
  Adder #(.width(32)) adder_2 (.a(PC4), .b(bit_extender_1_out), .out(adder_2_out));  // open: cin, cout
  Multiplexer #(.select(3), .width(32)) multiplexer_2 (
    .in0(PC4), .in1(beq_bgez), .in2({in_4[31:28], in_1, 2'b00}), .in3(in_5), .out(out_6), .sel(in_2));  // open: in4, in5, in6, in7, en

  // Other names for the same wires on the sheet: cmp = in_3; imm26[25:0] = in_1; j_jal[31:2] = {in_4[31:28], in_1};
  //   PC[31:0] = in_4; jr[31:0] = in_5; NPC[31:0] = out_6; NPCsel[2:0] = in_2
endmodule

module ALU (
  input  [3:0] in_1,
  input  [4:0] in_2,
  input  [31:0] in_3,
  input  [31:0] in_4,
  output [31:0] out_5,
  output out_6
);

  wire comparator_1_eq, comparator_2_lt, comparator_3_gt, not_1_out;
  wire [31:0] _000, _001, _010, _011, _100, _101, _110, _111;

  Adder #(.width(32)) adder_1 (.a(in_3), .b(in_4), .out(_000));  // open: cin, cout
  Subtractor #(.width(32)) subtractor_1 (.a(in_3), .b(in_4), .out(_001));  // open: bin, bout
  Shifter #(.width(32)) shifter_1 (.in(in_4), .\dist (in_2), .out(_010));
  Comparator #(.width(32)) comparator_1 (.a(in_3), .b(in_4), .eq(comparator_1_eq));  // open: gt, lt
  Comparator #(.width(32)) comparator_2 (.a(in_3), .b(in_4), .lt(comparator_2_lt));  // open: gt, eq
  Comparator #(.width(32)) comparator_3 (.a(in_3), .b({32{1'b0}}), .gt(comparator_3_gt));  // open: eq, lt
  assign _110 = in_3 | in_4;  // OR_Gate or_1, 32 bits wide
  assign _111 = in_3 & in_4;  // AND_Gate and_1, 32 bits wide
  assign _011 = {{31{1'b0}}, comparator_1_eq};  // Bit_Extender bit_extender_1
  assign _100 = {{31{1'b0}}, comparator_2_lt};  // Bit_Extender bit_extender_2
  not not_1 (not_1_out, comparator_3_gt);
  assign _101 = {{31{1'b0}}, not_1_out};  // Bit_Extender bit_extender_3
  Multiplexer #(.select(4), .width(32)) multiplexer_1 (
    .in0(_000), .in1(_001), .in2(_010), .in3(_011), .in4(_100), .in5(_101), .in6(_110), .in7(_111),
    .in15({32{1'b0}}), .out(out_5), .sel(in_1));  // open: in8, in9, in10, in11, in12, in13, in14, en

  assign out_6 = out_5[0];

  // Other names for the same wires on the sheet: A[31:0] = in_3; B[31:0] = in_4; CTRL[3:0] = in_1; Shamt[4:0] = in_2
endmodule

module DM (
  input  in_1,
  input  in_2,
  input  in_3,
  input  [4:0] in_4,
  input  [31:0] in_5,
  output [31:0] out_6
);

  RAM #(.addrWidth(5), .dataWidth(32), .bus("separate")) ram_1 (
    .addr(in_4), .din(in_5), .data(out_6), .str(in_1), .clk(in_2), .clr(in_3));  // open: sel, ld

  // Other names for the same wires on the sheet: clk = in_2; reset = in_3; WE = in_1
endmodule

module CTR (
  input  [31:0] in_1,
  output [2:0] out_2,
  output out_3,
  output [1:0] out_4,
  output [1:0] out_5,
  output [1:0] out_6,
  output [3:0] out_7,
  output out_8,
  output out_9,
  output [2:0] out_10,
  output [2:0] out_11
);

  wire addiu, addu, \and , beq, blez, comparator_13_eq, comparator_14_eq, comparator_15_eq, comparator_16_eq,
       comparator_17_eq, comparator_18_eq, j, jal, jr, lb, lui, lw, or_1_out, or_2_out, or_3_out, or_4_out,
       or_5_out, or_6_out, or_7_out, or_9_out, or_10_out, or_11_out, or_12_out, or_13_out, or_14_out,
       or_15_out, or_16_out, ori, priority_encoder_1_p9, sb, sll, slt, special, subu, sw;

  Comparator #(.width(6), .mode("unsigned")) comparator_1 (.a(6'b100011), .b(in_1[31:26]), .eq(lw));  // open: gt, lt
  Comparator #(.width(6), .mode("unsigned")) comparator_2 (.a(6'b000100), .b(in_1[31:26]), .eq(beq));  // open: gt, lt
  buf or_1 (or_1_out, \and );  // OR_Gate
  buf or_2 (or_2_out, ori);  // OR_Gate
  buf or_3 (or_3_out, blez);  // OR_Gate
  buf or_4 (or_4_out, slt);  // OR_Gate
  buf or_5 (or_5_out, beq);  // OR_Gate
  buf or_6 (or_6_out, sll);  // OR_Gate
  buf or_7 (or_7_out, subu);  // OR_Gate
  // Priority_Encoder #(.select(4)) priority_encoder_1: pin names not known; wires that end beside it: or_7_out, or_6_out, or_5_out, or_4_out, or_3_out, or_2_out, or_1_out, out_7, priority_encoder_1_p9
  Pull_Resistor pull_resistor_1 (.node(out_7));
  Comparator #(.width(6), .mode("unsigned")) comparator_3 (.a(6'b101011), .b(in_1[31:26]), .eq(sw));  // open: gt, lt
  Comparator #(.width(6), .mode("unsigned")) comparator_4 (.a(6'b000110), .b(in_1[31:26]), .eq(blez));  // open: gt, lt
  Comparator #(.width(6), .mode("unsigned")) comparator_5 (.a(6'b001111), .b(in_1[31:26]), .eq(lui));  // open: gt, lt
  buf or_8 (priority_encoder_1_p9, lui);  // OR_Gate
  buf or_9 (or_9_out, jr);  // OR_Gate
  or or_10 (or_10_out, j, jal);
  or or_11 (or_11_out, beq, blez);
  Comparator #(.width(6), .mode("unsigned")) comparator_6 (
    .a({6{1'b0}}), .b(in_1[31:26]), .eq(special));  // open: gt, lt
  Comparator #(.width(6), .mode("unsigned")) comparator_7 (.a(6'b001101), .b(in_1[31:26]), .eq(ori));  // open: gt, lt
  Comparator #(.width(6), .mode("unsigned")) comparator_8 (.a(6'b000010), .b(in_1[31:26]), .eq(j));  // open: gt, lt
  Comparator #(.width(6), .mode("unsigned")) comparator_9 (.a(6'b100000), .b(in_1[31:26]), .eq(lb));  // open: gt, lt
  // Priority_Encoder #(.disabled(0)) priority_encoder_2: pin names not known; wires that end beside it: or_11_out, or_10_out, or_9_out, out_2
  Pull_Resistor pull_resistor_2 (.node(out_2));
  Comparator #(.width(6), .mode("unsigned")) comparator_10 (
    .a(6'b001001), .b(in_1[31:26]), .eq(addiu));  // open: gt, lt
  Comparator #(.width(6), .mode("unsigned")) comparator_11 (.a(6'b000011), .b(in_1[31:26]), .eq(jal));  // open: gt, lt
  Comparator #(.width(6), .mode("unsigned")) comparator_12 (.a(6'b101000), .b(in_1[31:26]), .eq(sb));  // open: gt, lt
  buf or_12 (or_12_out, jal);  // OR_Gate
  // Priority_Encoder #(.select(2)) priority_encoder_3: pin names not known; wires that end beside it: special, out_4, or_12_out
  Pull_Resistor pull_resistor_3 (.node(out_4));
  Comparator #(.width(6), .mode("unsigned")) comparator_13 (
    .a(6'b100001), .b(in_1[5:0]), .eq(comparator_13_eq));  // open: gt, lt
  Comparator #(.width(6), .mode("unsigned")) comparator_14 (
    .a(6'b001000), .b(in_1[5:0]), .eq(comparator_14_eq));  // open: gt, lt
  Comparator #(.width(6), .mode("unsigned")) comparator_15 (
    .a(6'b100100), .b(in_1[5:0]), .eq(comparator_15_eq));  // open: gt, lt
  buf or_13 (or_13_out, lui);  // OR_Gate
  or or_14 (or_14_out, lw, sw, sb, lb, addiu);
  // Priority_Encoder #(.select(2)) priority_encoder_4: pin names not known; wires that end beside it: or_14_out, out_6, or_13_out
  Pull_Resistor pull_resistor_4 (.node(out_6));
  buf or_15 (or_15_out, jal);  // OR_Gate
  or or_16 (or_16_out, lw, lb);
  // Priority_Encoder #(.select(2)) priority_encoder_5: pin names not known; wires that end beside it: or_16_out, out_5, or_15_out, lui
  Pull_Resistor pull_resistor_5 (.node(out_5));
  and and_1 (addu, comparator_13_eq, special);
  and and_2 (jr, comparator_14_eq, special);
  and and_3 (\and , comparator_15_eq, special);
  Comparator #(.width(6), .mode("unsigned")) comparator_16 (
    .a({6{1'b0}}), .b(in_1[5:0]), .eq(comparator_16_eq));  // open: gt, lt
  Comparator #(.width(6), .mode("unsigned")) comparator_17 (
    .a(6'b101010), .b(in_1[5:0]), .eq(comparator_17_eq));  // open: gt, lt
  Comparator #(.width(6), .mode("unsigned")) comparator_18 (
    .a(6'b100011), .b(in_1[5:0]), .eq(comparator_18_eq));  // open: gt, lt
  // Priority_Encoder #(.disabled(0)) priority_encoder_6: pin names not known; wires that end beside it: lb, out_11
  Pull_Resistor pull_resistor_6 (.node(out_11));
  // Priority_Encoder #(.disabled(0)) priority_encoder_7: pin names not known; wires that end beside it: sb, out_10
  Pull_Resistor pull_resistor_7 (.node(out_10));
  and and_4 (sll, comparator_16_eq, special);
  and and_5 (slt, comparator_17_eq, special);
  and and_6 (subu, comparator_18_eq, special);
  or or_17 (out_3, lb, addu, sll, slt, lw, ori, jal, addiu, \and , subu, lui);
  or or_18 (out_9, sb, sw);
  or or_19 (out_8, lw, sw, ori, addiu, lb, sb);

  // Other names for the same wires on the sheet: ALU_B_sel = out_8; ALU_op[3:0] = out_7; DM_wr = out_9;
  //   EXT_op[1:0] = out_6; func[5:0] = in_1[5:0]; opcode[5:0] = in_1[31:26]; MR_op[2:0] = out_11; MW_op[2:0] = out_10;
  //   NPC_op[2:0] = out_2; RF_A3_sel[1:0] = out_4; RF_WD_sel[1:0] = out_5; RF_wr = out_3
endmodule

module EXT (
  input  [1:0] in_1,
  input  [15:0] in_2,
  output [31:0] out_3
);

  wire [31:0] bit_extender_1_out, bit_extender_2_out;

  assign bit_extender_1_out = {{16{1'b0}}, in_2};  // Bit_Extender bit_extender_1
  assign bit_extender_2_out = {{16{in_2[15]}}, in_2};  // Bit_Extender bit_extender_2
  Multiplexer #(.select(2), .width(32), .enable("false")) multiplexer_1 (
    .in0(bit_extender_1_out), .in1(bit_extender_2_out), .in2({in_2, {16{1'b0}}}), .out(out_3), .sel(in_1));  // open: in3
endmodule

module SPLT (
  input  [31:0] in_1,
  output [25:0] out_2,
  output [15:0] out_3,
  output [4:0] out_4,
  output [4:0] out_5,
  output [4:0] out_6,
  output [4:0] out_7
);


  assign out_2 = in_1[25:0];
  assign out_3 = in_1[15:0];
  assign out_4 = in_1[25:21];
  assign out_5 = in_1[20:16];
  assign out_6 = in_1[15:11];
  assign out_7 = in_1[10:6];
endmodule

module MW (
  input  [2:0] in_1,
  input  [31:0] in_2,
  input  [31:0] in_3,
  input  [31:0] in_4,
  output [31:0] Out
);

  wire [31:0] sb;

  Multiplexer #(.select(2), .width(32)) multiplexer_1 (
    .in0({in_2[31:8], in_4[7:0]}), .in1({in_2[31:16], in_4[7:0], in_2[7:0]}),
    .in2({in_2[31:24], in_4[7:0], in_2[15:0]}), .in3({in_4[7:0], in_2[23:0]}), .out(sb), .sel(in_3[1:0]));  // open: en
  Multiplexer #(.select(3), .width(32)) multiplexer_2 (
    .in0(in_4), .in1(sb), .out(Out), .sel(in_1));  // open: in2, in3, in4, in5, in6, in7, en

  // Other names for the same wires on the sheet: _00[31:0] = {in_2[31:8], in_4[7:0]};
  //   _01[31:0] = {in_2[31:16], in_4[7:0], in_2[7:0]}; _11[31:0] = {in_4[7:0], in_2[23:0]}; Mem[31:0] = in_2;
  //   _10[31:0] = {in_2[31:24], in_4[7:0], in_2[15:0]}; sw[31:0] = in_4; WD[31:0] = in_4; A[31:0] = in_3;
  //   byte[1:0] = in_3[1:0]; MW_op[2:0] = in_1
endmodule

module MR (
  input  [2:0] in_1,
  input  [31:0] in_2,
  input  [31:0] in_3,
  output [31:0] Out
);

  wire [31:0] _00, _01, _10, _11, lb;

  assign _00 = {{24{in_3[7]}}, in_3[7:0]};  // Bit_Extender bit_extender_1
  assign _01 = {{24{in_3[15]}}, in_3[15:8]};  // Bit_Extender bit_extender_2
  assign _10 = {{24{in_3[23]}}, in_3[23:16]};  // Bit_Extender bit_extender_3
  assign _11 = {{24{in_3[31]}}, in_3[31:24]};  // Bit_Extender bit_extender_4
  Multiplexer #(.select(2), .width(32)) multiplexer_1 (
    .in0(_00), .in1(_01), .in2(_10), .in3(_11), .out(lb), .sel(in_2[1:0]));  // open: en
  Multiplexer #(.select(3), .width(32)) multiplexer_2 (
    .in0(in_3), .in1(lb), .out(Out), .sel(in_1));  // open: in2, in3, in4, in5, in6, in7, en

  // Other names for the same wires on the sheet: A[31:0] = in_2; byte[1:0] = in_2[1:0]; lw[31:0] = in_3;
  //   Mem[31:0] = in_3; MR_op[2:0] = in_1
endmodule
